// Logisim project lab_08.circ as structural Verilog: 1 circuit, main circuit main
module main (
  input  [7:0] Input,
  input  [7:0] One_Constant,
  output [7:0] Output
);

  wire [7:0] not_1_out;

  assign not_1_out = ~Input;  // NOT_Gate not_1, 8 bits wide
  Adder adder_1 (.a(not_1_out), .b(One_Constant), .out(Output));  // open: cin, cout
endmodule
