// Logisim project lab9.circ as structural Verilog: 7 circuits, main circuit main
module main (
  input  control_1,
  input  control_2,
  input  [3:0] A,
  input  [3:0] B,
  output [3:0] Output
);

  wire [3:0] n4_bit_nand_1_output, n4_bit_nor_1_output, n4_bit_xnor_1_output, n4_bit_xor_1_output;

  _4_bit_xor u_4_bit_xor_1 (.A(A), .B(B), .Output(n4_bit_xor_1_output));
  _4_bit_nand u_4_bit_nand_1 (.A(A), .B(B), .Output(n4_bit_nand_1_output));
  _4_bit_xnor u_4_bit_xnor_1 (.A(A), .B(B), .Output(n4_bit_xnor_1_output));
  _4_bit_nor u_4_bit_nor_1 (.A(A), .B(B), .Output(n4_bit_nor_1_output));
  _4_bit_4x1_mux u_4_bit_4x1_mux_1 (
    .D0(n4_bit_xor_1_output), .D1(n4_bit_nand_1_output), .D2(n4_bit_xnor_1_output), .D3(n4_bit_nor_1_output),
    .S0(control_1), .S1(control_2), .Output(Output));
endmodule

// XOR
module _4_bit_xor (
  input  [3:0] A,
  input  [3:0] B,
  output [3:0] Output
);

  xor xor_1 (Output[0], A[0], B[0]);
  xor xor_2 (Output[1], A[1], B[1]);
  xor xor_3 (Output[2], A[2], B[2]);
  xor xor_4 (Output[3], A[3], B[3]);
endmodule

// NAND
module _4_bit_nand (
  input  [3:0] A,
  input  [3:0] B,
  output [3:0] Output
);

  nand nand_1 (Output[0], A[0], B[0]);
  nand nand_2 (Output[1], A[1], B[1]);
  nand nand_3 (Output[2], A[2], B[2]);
  nand nand_4 (Output[3], A[3], B[3]);
endmodule

// XNOR
module _4_bit_xnor (
  input  [3:0] A,
  input  [3:0] B,
  output [3:0] Output
);

  xnor xnor_1 (Output[0], A[0], B[0]);
  xnor xnor_2 (Output[1], A[1], B[1]);
  xnor xnor_3 (Output[2], A[2], B[2]);
  xnor xnor_4 (Output[3], A[3], B[3]);
endmodule

// NOR
module _4_bit_nor (
  input  [3:0] A,
  input  [3:0] B,
  output [3:0] Output
);

  nor nor_1 (Output[0], A[0], B[0]);
  nor nor_2 (Output[1], A[1], B[1]);
  nor nor_3 (Output[2], A[2], B[2]);
  nor nor_4 (Output[3], A[3], B[3]);
endmodule

// MUX
module _1_bit_4x1_mux (
  input  S1,
  input  S2,
  input  D0,
  input  D1,
  input  D2,
  input  D0_2,
  output Output
);

  wire and_1_out, and_2_out, and_3_out, and_4_out, not_1_out, not_2_out;

  not not_1 (not_1_out, S1);
  not not_2 (not_2_out, S2);
  and and_1 (and_1_out, not_1_out, D0, not_2_out);
  and and_2 (and_2_out, not_1_out, D1, S2);
  and and_3 (and_3_out, S1, D2, not_2_out);
  and and_4 (and_4_out, S1, D0_2, S2);
  or or_1 (Output, and_1_out, and_2_out, and_3_out, and_4_out);
endmodule

// MUX
module _4_bit_4x1_mux (
  input  S0,
  input  S1,
  input  [3:0] D0,
  input  [3:0] D1,
  input  [3:0] D2,
  input  [3:0] D3,
  output [3:0] Output
);

  _1_bit_4x1_mux u_1_bit_4x1_mux_1 (
    .D0(D0[0]), .D1(D1[0]), .D2(D2[0]), .D0_2(D3[0]), .S1(S0), .S2(S1), .Output(Output[0]));
  _1_bit_4x1_mux u_1_bit_4x1_mux_2 (
    .D0(D0[1]), .D1(D1[1]), .D2(D2[1]), .D0_2(D3[1]), .S1(S0), .S2(S1), .Output(Output[1]));
  _1_bit_4x1_mux u_1_bit_4x1_mux_3 (
    .D0(D0[2]), .D1(D1[2]), .D2(D2[2]), .D0_2(D3[2]), .S1(S0), .S2(S1), .Output(Output[2]));
  _1_bit_4x1_mux u_1_bit_4x1_mux_4 (
    .D0(D0[3]), .D1(D1[3]), .D2(D2[3]), .D0_2(D3[3]), .S1(S0), .S2(S1), .Output(Output[3]));
endmodule
