// Logisim project lab10.circ as structural Verilog: 6 circuits, main circuit main
module main (
  input  [3:0] Shift,
  input  [3:0] Number,
  output [3:0] Output
);

  _4_bit_shifter u_4_bit_shifter_1 (.Number(Number), .Shift(Shift), .Output(Output));
endmodule

module _4_bit_shifter (
  input  [3:0] Number,
  input  [3:0] Shift,
  output [3:0] Output
);

  wire [3:0] n1_bit_left_shift_1_output, n2_bit_left_shift_1_output, n3_bit_left_shift_1_output;

  _1_bit_left_shift u_1_bit_left_shift_1 (.Input(Number), .Output(n1_bit_left_shift_1_output));
  _2_bit_left_shift u_2_bit_left_shift_1 (.Input(Number), .Output(n2_bit_left_shift_1_output));
  _3_bit_left_shift u_3_bit_left_shift_1 (.Input(Number), .Output(n3_bit_left_shift_1_output));
  _4_bit_4x1_mux u_4_bit_4x1_mux_1 (
    .D0(Number), .D1(n1_bit_left_shift_1_output), .D2(n2_bit_left_shift_1_output),
    .D3(n3_bit_left_shift_1_output), .S0(Shift[1]), .S1(Shift[0]), .Output(Output));
endmodule

// 1
module _1_bit_left_shift (
  input  [3:0] Input,
  output [3:0] Output
);


  assign Output = {Input[2:0], 1'b0};
endmodule

// 2
module _2_bit_left_shift (
  input  [3:0] Input,
  output [3:0] Output
);

  wire [3:0] n1_bit_left_shift_1_output;

  _1_bit_left_shift u_1_bit_left_shift_1 (.Input(Input), .Output(n1_bit_left_shift_1_output));
  _1_bit_left_shift u_1_bit_left_shift_2 (.Input(n1_bit_left_shift_1_output), .Output(Output));
endmodule

// 3
module _3_bit_left_shift (
  input  [3:0] Input,
  output [3:0] Output
);

  wire [3:0] n1_bit_left_shift_1_output, n1_bit_left_shift_2_output;

  _1_bit_left_shift u_1_bit_left_shift_1 (.Input(Input), .Output(n1_bit_left_shift_1_output));
  _1_bit_left_shift u_1_bit_left_shift_2 (.Input(n1_bit_left_shift_1_output), .Output(n1_bit_left_shift_2_output));
  _1_bit_left_shift u_1_bit_left_shift_3 (.Input(n1_bit_left_shift_2_output), .Output(Output));
endmodule

// 4
module _4_bit_left_shift (
  input  [3:0] Input,
  output [3:0] Output
);

  wire [3:0] n1_bit_left_shift_1_output, n1_bit_left_shift_2_output, n1_bit_left_shift_3_output;

  _1_bit_left_shift u_1_bit_left_shift_1 (.Input(Input), .Output(n1_bit_left_shift_1_output));
  _1_bit_left_shift u_1_bit_left_shift_2 (.Input(n1_bit_left_shift_3_output), .Output(n1_bit_left_shift_2_output));
  _1_bit_left_shift u_1_bit_left_shift_3 (.Input(n1_bit_left_shift_1_output), .Output(n1_bit_left_shift_3_output));
  _1_bit_left_shift u_1_bit_left_shift_4 (.Input(n1_bit_left_shift_2_output), .Output(Output));
endmodule
