// Logisim project proj4.circ as structural Verilog: 21 circuits, main circuit main
module main (
  input  [2:0] Control,
  input  [7:0] A,
  input  [7:0] B,
  output [7:0] Result,
  output Zero,
  output Negative,
  output Carry,
  output Overflow
);

  wire ADD_carry_out, ADD_overflow, n8_bit_div_1_carry, n8_bit_div_1_overflow, n8_bit_mul_1_carry,
       n8_bit_mul_1_overflow, n8_bit_shl_1_carry, n8_bit_shr_1_carry, or_1_out, SUB_carry_out, SUB_overflow;
  wire [7:0] ADD_result, n8_bit_and_1_result, n8_bit_div_1_quotient, n8_bit_mul_1_out_3, n8_bit_or_1_result,
       n8_bit_shl_1_output, n8_bit_shr_1_output, SUB_result;

  _8_bit_shl u_8_bit_shl_1 (.Shift_By(B), .Number(A), .Output(n8_bit_shl_1_output), .Carry(n8_bit_shl_1_carry));
  _8_bit_shr u_8_bit_shr_1 (.Shift_By(B), .Number(A), .Output(n8_bit_shr_1_output), .Carry(n8_bit_shr_1_carry));
  _8_bit_mul u_8_bit_mul_1 (
    .A(A), .B(B), .out_3(n8_bit_mul_1_out_3), .Carry(n8_bit_mul_1_carry), .Overflow(n8_bit_mul_1_overflow));
  _8_bit_div u_8_bit_div_1 (
    .Dividend(A), .Divisior(B), .Quotient(n8_bit_div_1_quotient), .Overflow(n8_bit_div_1_overflow),
    .Carry(n8_bit_div_1_carry));
  _8_bit_AND u_8_bit_and_1 (.Result(n8_bit_and_1_result), .A(A), .B(B));
  _8_bit_OR u_8_bit_or_1 (.Result(n8_bit_or_1_result), .A(A), .B(B));
  _8_bit_Adder_Subtracter ADD (
    .Add_Sub_Control(1'b0), .Result(ADD_result), .A(A), .B(B), .Carry_out(ADD_carry_out),
    .Overflow(ADD_overflow));
  _8_bit_Adder_Subtracter SUB (
    .Add_Sub_Control(1'b1), .Result(SUB_result), .A(A), .B(B), .Carry_out(SUB_carry_out),
    .Overflow(SUB_overflow));
  _8_bit_8x1_mux u_8_bit_8x1_mux_1 (
    .D1(n8_bit_and_1_result), .D2(n8_bit_or_1_result), .D3(ADD_result), .D4(SUB_result),
    .D5(n8_bit_shl_1_output), .D6(n8_bit_shr_1_output), .D7(n8_bit_mul_1_out_3), .D8(n8_bit_div_1_quotient),
    .Selector(Control), .Output({Negative, Result[6:0]}));
  _1_bit_8x1_mux u_1_bit_8x1_mux_1 (
    .D1(1'b0), .D2(1'b0), .D3(ADD_carry_out), .D4(SUB_carry_out), .D5(n8_bit_shl_1_carry),
    .D6(n8_bit_shr_1_carry), .D7(n8_bit_mul_1_overflow), .D8(n8_bit_div_1_carry), .S1(Control), .Output(Carry));
  _1_bit_8x1_mux u_1_bit_8x1_mux_2 (
    .D1(1'b0), .D2(1'b0), .D3(ADD_overflow), .D4(SUB_overflow), .D5(1'b0), .D6(1'b0),
    .D7(n8_bit_mul_1_carry), .D8(n8_bit_div_1_overflow), .S1(Control), .Output(Overflow));
  or or_1 (or_1_out, Result[0], Result[1], Result[2], Result[3], Result[4], Result[5], Result[6], Negative);
  not not_1 (Zero, or_1_out);

  assign Result[7] = Negative;

  // Notes on the sheet:
  //   AND
  //   OR
  //   Full 8-bit ALU
endmodule

// +
module _1_bit_Adder (
  input  Carry_In,
  input  A,
  input  B,
  output Result,
  output Carry_Out
);

  wire and_1_out, and_2_out, xor_1_out;

  and and_1 (and_1_out, A, B);
  xor xor_1 (xor_1_out, A, B);
  or or_1 (Carry_Out, and_1_out, and_2_out);
  and and_2 (and_2_out, Carry_In, xor_1_out);
  xor xor_2 (Result, Carry_In, xor_1_out);

  // Notes on the sheet:
  //   Full Adder
endmodule

// +/-
module _8_bit_Adder_Subtracter (
  input  Add_Sub_Control,
  input  [7:0] A,
  input  [7:0] B,
  output [7:0] Result,
  output Carry_out,
  output Overflow
);

  wire and_1_out, and_2_out, n1_bit_adder_1_carry_out, n1_bit_adder_2_carry_out, n1_bit_adder_3_carry_out,
       n1_bit_adder_4_carry_out, n1_bit_adder_5_carry_out, n1_bit_adder_6_carry_out,
       n1_bit_adder_7_carry_out, not_1_out, not_2_out, not_3_out, xor_1_out, xor_2_out, xor_3_out, xor_4_out,
       xor_5_out, xor_6_out, xor_7_out, xor_8_out;

  xor xor_1 (xor_1_out, Add_Sub_Control, B[0]);
  xor xor_2 (xor_2_out, Add_Sub_Control, B[1]);
  xor xor_3 (xor_3_out, Add_Sub_Control, B[2]);
  xor xor_4 (xor_4_out, Add_Sub_Control, B[3]);
  xor xor_5 (xor_5_out, Add_Sub_Control, B[4]);
  xor xor_6 (xor_6_out, Add_Sub_Control, B[5]);
  xor xor_7 (xor_7_out, Add_Sub_Control, B[6]);
  xor xor_8 (xor_8_out, Add_Sub_Control, B[7]);
  not not_1 (not_1_out, xor_8_out);
  not not_2 (not_2_out, A[7]);
  _1_bit_Adder u_1_bit_adder_1 (
    .A(A[0]), .B(xor_1_out), .Result(Result[0]), .Carry_Out(n1_bit_adder_1_carry_out),
    .Carry_In(Add_Sub_Control));
  _1_bit_Adder u_1_bit_adder_2 (
    .A(A[1]), .B(xor_2_out), .Result(Result[1]), .Carry_Out(n1_bit_adder_2_carry_out),
    .Carry_In(n1_bit_adder_1_carry_out));
  _1_bit_Adder u_1_bit_adder_3 (
    .A(A[2]), .B(xor_3_out), .Result(Result[2]), .Carry_Out(n1_bit_adder_3_carry_out),
    .Carry_In(n1_bit_adder_2_carry_out));
  _1_bit_Adder u_1_bit_adder_4 (
    .A(A[3]), .B(xor_4_out), .Result(Result[3]), .Carry_Out(n1_bit_adder_4_carry_out),
    .Carry_In(n1_bit_adder_3_carry_out));
  _1_bit_Adder u_1_bit_adder_5 (
    .A(A[4]), .B(xor_5_out), .Result(Result[4]), .Carry_Out(n1_bit_adder_5_carry_out),
    .Carry_In(n1_bit_adder_4_carry_out));
  _1_bit_Adder u_1_bit_adder_6 (
    .A(A[5]), .B(xor_6_out), .Result(Result[5]), .Carry_Out(n1_bit_adder_6_carry_out),
    .Carry_In(n1_bit_adder_5_carry_out));
  _1_bit_Adder u_1_bit_adder_7 (
    .A(A[6]), .B(xor_7_out), .Result(Result[6]), .Carry_Out(n1_bit_adder_7_carry_out),
    .Carry_In(n1_bit_adder_6_carry_out));
  _1_bit_Adder u_1_bit_adder_8 (
    .A(A[7]), .B(xor_8_out), .Result(Result[7]), .Carry_Out(Carry_out), .Carry_In(n1_bit_adder_7_carry_out));
  not not_3 (not_3_out, Result[7]);
  and and_1 (and_1_out, Result[7], not_2_out, not_1_out);
  and and_2 (and_2_out, not_3_out, A[7], xor_8_out);
  or or_1 (Overflow, and_1_out, and_2_out);

  // Notes on the sheet:
  //   8-bit Adder/Subtractor
endmodule

module _8_bit_AND (
  input  [7:0] A,
  input  [7:0] B,
  output [7:0] Result
);

  and AND (Result[0], A[0], B[0]);
  and AND_2 (Result[1], A[1], B[1]);
  and AND_3 (Result[2], A[2], B[2]);
  and AND_4 (Result[3], A[3], B[3]);
  and AND_5 (Result[4], A[4], B[4]);
  and AND_6 (Result[5], A[5], B[5]);
  and AND_7 (Result[6], A[6], B[6]);
  and AND_8 (Result[7], A[7], B[7]);

  // Notes on the sheet:
  //   8-bit AND
endmodule

module _8_bit_OR (
  input  [7:0] A,
  input  [7:0] B,
  output [7:0] Result
);

  or OR (Result[0], A[0], B[0]);
  or OR_2 (Result[1], A[1], B[1]);
  or OR_3 (Result[2], A[2], B[2]);
  or OR_4 (Result[3], A[3], B[3]);
  or OR_5 (Result[4], A[4], B[4]);
  or OR_6 (Result[5], A[5], B[5]);
  or OR_7 (Result[6], A[6], B[6]);
  or OR_8 (Result[7], A[7], B[7]);

  // Notes on the sheet:
  //   8-bit OR
endmodule

module _8_bit_mux (
  input  Control_Pin,
  input  [7:0] A,
  input  [7:0] B,
  output [7:0] Output
);

  _1_bit_2x1_mux u_1_bit_2x1_mux_1 (.D1(A[0]), .D2(B[0]), .S1(Control_Pin), .Output(Output[0]));
  _1_bit_2x1_mux u_1_bit_2x1_mux_2 (.D1(A[1]), .D2(B[1]), .S1(Control_Pin), .Output(Output[1]));
  _1_bit_2x1_mux u_1_bit_2x1_mux_3 (.D1(A[2]), .D2(B[2]), .S1(Control_Pin), .Output(Output[2]));
  _1_bit_2x1_mux u_1_bit_2x1_mux_4 (.D1(A[3]), .D2(B[3]), .S1(Control_Pin), .Output(Output[3]));
  _1_bit_2x1_mux u_1_bit_2x1_mux_5 (.D1(A[4]), .D2(B[4]), .S1(Control_Pin), .Output(Output[4]));
  _1_bit_2x1_mux u_1_bit_2x1_mux_6 (.D1(A[5]), .D2(B[5]), .S1(Control_Pin), .Output(Output[5]));
  _1_bit_2x1_mux u_1_bit_2x1_mux_7 (.D1(A[6]), .D2(B[6]), .S1(Control_Pin), .Output(Output[6]));
  _1_bit_2x1_mux u_1_bit_2x1_mux_8 (.D1(A[7]), .D2(B[7]), .S1(Control_Pin), .Output(Output[7]));

  // Other names for the same wires on the sheet: _0_0 = A[0]; _0_1 = A[1]; _0_2 = A[2]; _0_3 = A[3]; _0_4 = A[4];
  //   _0_5 = A[5]; _0_6 = A[6]; _0_7 = A[7]; _1_0 = B[0]; _1_1 = B[1]; _1_2 = B[2]; _1_3 = B[3]; _1_4 = B[4];
  //   _1_5 = B[5]; _1_6 = B[6]; _1_7 = B[7]
endmodule

module _8_bit_8x1_mux (
  input  [2:0] Selector,
  input  [7:0] D1,
  input  [7:0] D2,
  input  [7:0] D3,
  input  [7:0] D4,
  input  [7:0] D5,
  input  [7:0] D6,
  input  [7:0] D7,
  input  [7:0] D8,
  output [7:0] Output
);

  _1_bit_8x1_mux BIT_0 (
    .D1(D1[0]), .D2(D2[0]), .D3(D3[0]), .D4(D4[0]), .D5(D5[0]), .D6(D6[0]), .D7(D7[0]), .D8(D8[0]),
    .S1(Selector), .Output(Output[0]));
  _1_bit_8x1_mux BIT_1 (
    .D1(D1[1]), .D2(D2[1]), .D3(D3[1]), .D4(D4[1]), .D5(D5[1]), .D6(D6[1]), .D7(D7[1]), .D8(D8[1]),
    .S1(Selector), .Output(Output[1]));
  _1_bit_8x1_mux Bit_2 (
    .D1(D1[2]), .D2(D2[2]), .D3(D3[2]), .D4(D4[2]), .D5(D5[2]), .D6(D6[2]), .D7(D7[2]), .D8(D8[2]),
    .S1(Selector), .Output(Output[2]));
  _1_bit_8x1_mux Bit_3 (
    .D1(D1[3]), .D2(D2[3]), .D3(D3[3]), .D4(D4[3]), .D5(D5[3]), .D6(D6[3]), .D7(D7[3]), .D8(D8[3]),
    .S1(Selector), .Output(Output[3]));
  _1_bit_8x1_mux u_1_bit_8x1_mux_1 (
    .D1(D1[4]), .D2(D2[4]), .D3(D3[4]), .D4(D4[4]), .D5(D5[4]), .D6(D6[4]), .D7(D7[4]), .D8(D8[4]),
    .S1(Selector), .Output(Output[4]));
  _1_bit_8x1_mux u_1_bit_8x1_mux_2 (
    .D1(D1[5]), .D2(D2[5]), .D3(D3[5]), .D4(D4[5]), .D5(D5[5]), .D6(D6[5]), .D7(D7[5]), .D8(D8[5]),
    .S1(Selector), .Output(Output[5]));
  _1_bit_8x1_mux u_1_bit_8x1_mux_3 (
    .D1(D1[6]), .D2(D2[6]), .D3(D3[6]), .D4(D4[6]), .D5(D5[6]), .D6(D6[6]), .D7(D7[6]), .D8(D8[6]),
    .S1(Selector), .Output(Output[6]));
  _1_bit_8x1_mux u_1_bit_8x1_mux_4 (
    .D1(D1[7]), .D2(D2[7]), .D3(D3[7]), .D4(D4[7]), .D5(D5[7]), .D6(D6[7]), .D7(D7[7]), .D8(D8[7]),
    .S1(Selector), .Output(Output[7]));
endmodule

// 8x1 MUX
module _1_bit_8x1_mux (
  input  [2:0] S1,
  input  D1,
  input  D2,
  input  D3,
  input  D4,
  input  D5,
  input  D6,
  input  D7,
  input  D8,
  output Output
);

  wire and_1_out, and_2_out, and_3_out, and_4_out, and_5_out, and_6_out, and_7_out, and_8_out, not_1_out,
       not_2_out, not_3_out, or_1_out, or_2_out;

  not not_1 (not_1_out, S1[2]);
  not not_2 (not_2_out, S1[1]);
  not not_3 (not_3_out, S1[0]);
  and and_1 (and_1_out, D1, not_3_out, not_2_out, not_1_out);
  and and_2 (and_2_out, D2, S1[0], not_2_out, not_1_out);
  and and_3 (and_3_out, D3, not_3_out, S1[1], not_1_out);
  and and_4 (and_4_out, D4, S1[0], S1[1], not_1_out);
  and and_5 (and_5_out, D5, not_3_out, not_2_out, S1[2]);
  and and_6 (and_6_out, D6, S1[0], not_2_out, S1[2]);
  and and_7 (and_7_out, D7, not_3_out, S1[1], S1[2]);
  and and_8 (and_8_out, D8, S1[0], S1[1], S1[2]);
  or or_1 (or_1_out, and_1_out, and_2_out, and_3_out, and_4_out);
  or or_2 (or_2_out, and_5_out, and_6_out, and_7_out, and_8_out);
  or or_3 (Output, or_1_out, or_2_out);
endmodule

module _8_bit_8x1_testing (
  input  [2:0] Selector,
  input  [7:0] D1,
  input  [7:0] D2,
  input  [7:0] D3,
  input  [7:0] D4,
  input  [7:0] D5,
  input  [7:0] D6,
  input  [7:0] D7,
  input  [7:0] D8,
  output [7:0] Output
);

  _8_bit_8x1_mux u_8_bit_8x1_mux_1 (
    .D1(D1), .D2(D2), .D3(D3), .D4(D4), .D5(D5), .D6(D6), .D7(D7), .D8(D8), .Selector(Selector),
    .Output(Output));
endmodule

// SHL
module _8_bit_shl (
  input  [7:0] Shift_By,
  input  [7:0] Number,
  output [7:0] Output,
  output Carry
);

  wire n1_1_carry_out, n1_8_carry_out, n1_9_carry_out, n1_19_carry_out, n1_20_carry_out, n1_26_carry_out,
       n1_27_carry_out, not_1_out, or_1_out;
  wire [7:0] n1_1_out_2, n1_2_out_2, n1_3_out_2, n1_4_out_2, n1_5_out_2, n1_6_out_2, n1_7_out_2, n1_8_out_2,
       n1_9_out_2, n1_10_out_2, n1_11_out_2, n1_12_out_2, n1_13_out_2, n1_14_out_2, n1_15_out_2, n1_16_out_2,
       n1_17_out_2, n1_18_out_2, n1_19_out_2, n1_20_out_2, n1_21_out_2, n1_22_out_2, n1_23_out_2,
       n1_24_out_2, n1_25_out_2, n1_26_out_2, n1_27_out_2, n1_28_out_2, n8_bit_8x1_mux_1_output;

  _1 u_1_1 (.Number(Number), .out_2(n1_1_out_2), .Carry_out(n1_1_carry_out));
  _1 u_1_2 (.Number(Number), .out_2(n1_2_out_2));  // open: Carry_out
  _1 u_1_3 (.Number(Number), .out_2(n1_3_out_2));  // open: Carry_out
  _1 u_1_4 (.Number(Number), .out_2(n1_4_out_2));  // open: Carry_out
  _1 u_1_5 (.Number(Number), .out_2(n1_5_out_2));  // open: Carry_out
  _1 u_1_6 (.Number(Number), .out_2(n1_6_out_2));  // open: Carry_out
  _1 u_1_7 (.Number(Number), .out_2(n1_7_out_2));  // open: Carry_out
  _1 u_1_8 (.Number(n1_2_out_2), .out_2(n1_8_out_2), .Carry_out(n1_8_carry_out));
  _1 u_1_9 (.Number(n1_10_out_2), .out_2(n1_9_out_2), .Carry_out(n1_9_carry_out));
  _1 u_1_10 (.Number(n1_3_out_2), .out_2(n1_10_out_2));  // open: Carry_out
  _1 u_1_11 (.Number(n1_12_out_2), .out_2(n1_11_out_2));  // open: Carry_out
  _1 u_1_12 (.Number(n1_4_out_2), .out_2(n1_12_out_2));  // open: Carry_out
  _1 u_1_13 (.Number(n1_14_out_2), .out_2(n1_13_out_2));  // open: Carry_out
  _1 u_1_14 (.Number(n1_5_out_2), .out_2(n1_14_out_2));  // open: Carry_out
  _1 u_1_15 (.Number(n1_6_out_2), .out_2(n1_15_out_2));  // open: Carry_out
  _1 u_1_16 (.Number(n1_15_out_2), .out_2(n1_16_out_2));  // open: Carry_out
  _1 u_1_17 (.Number(n1_7_out_2), .out_2(n1_17_out_2));  // open: Carry_out
  _1 u_1_18 (.Number(n1_17_out_2), .out_2(n1_18_out_2));  // open: Carry_out
  or or_1 (or_1_out, Shift_By[3], Shift_By[4], Shift_By[5], Shift_By[6], Shift_By[7]);
  _1 u_1_19 (.Number(n1_11_out_2), .out_2(n1_19_out_2), .Carry_out(n1_19_carry_out));
  _1 u_1_20 (.Number(n1_21_out_2), .out_2(n1_20_out_2), .Carry_out(n1_20_carry_out));
  _1 u_1_21 (.Number(n1_13_out_2), .out_2(n1_21_out_2));  // open: Carry_out
  _1 u_1_22 (.Number(n1_23_out_2), .out_2(n1_22_out_2));  // open: Carry_out
  _1 u_1_23 (.Number(n1_16_out_2), .out_2(n1_23_out_2));  // open: Carry_out
  _1 u_1_24 (.Number(n1_18_out_2), .out_2(n1_24_out_2));  // open: Carry_out
  _1 u_1_25 (.Number(n1_24_out_2), .out_2(n1_25_out_2));  // open: Carry_out
  not not_1 (not_1_out, or_1_out);
  _1 u_1_26 (.Number(n1_22_out_2), .out_2(n1_26_out_2), .Carry_out(n1_26_carry_out));
  _1 u_1_27 (.Number(n1_28_out_2), .out_2(n1_27_out_2), .Carry_out(n1_27_carry_out));
  _1 u_1_28 (.Number(n1_25_out_2), .out_2(n1_28_out_2));  // open: Carry_out
  _8_bit_8x1_mux u_8_bit_8x1_mux_1 (
    .D1(Number), .D2(n1_1_out_2), .D3(n1_8_out_2), .D4(n1_9_out_2), .D5(n1_19_out_2), .D6(n1_20_out_2),
    .D7(n1_26_out_2), .D8(n1_27_out_2), .Selector(Shift_By[2:0]), .Output(n8_bit_8x1_mux_1_output));
  _1_bit_8x1_mux u_1_bit_8x1_mux_1 (
    .D1(1'b0), .D2(n1_1_carry_out), .D3(n1_8_carry_out), .D4(n1_9_carry_out), .D5(n1_19_carry_out),
    .D6(n1_20_carry_out), .D7(n1_26_carry_out), .D8(n1_27_carry_out), .S1(Shift_By[2:0]), .Output(Carry));
  Zeroer zeroer_1 (.Zero(not_1_out), .Number(n8_bit_8x1_mux_1_output), .Output(Output));
endmodule

// SHR
module _8_bit_shr (
  input  [7:0] Shift_By,
  input  [7:0] Number,
  output [7:0] Output,
  output Carry
);

  wire n1_1_carry_out, n1_8_carry_out, n1_9_carry_out, n1_19_carry_out, n1_20_carry_out, n1_26_carry_out,
       n1_28_carry_out, not_1_out, or_1_out;
  wire [7:0] n1_1_out, n1_2_out, n1_3_out, n1_4_out, n1_5_out, n1_6_out, n1_7_out, n1_8_out, n1_9_out,
       n1_10_out, n1_11_out, n1_12_out, n1_13_out, n1_14_out, n1_15_out, n1_16_out, n1_17_out, n1_18_out,
       n1_19_out, n1_20_out, n1_21_out, n1_22_out, n1_23_out, n1_24_out, n1_25_out, n1_26_out, n1_27_out,
       n1_28_out, n8_bit_8x1_mux_1_output;

  _1_2 u_1_1 (.Input(Number), .Out(n1_1_out), .Carry_out(n1_1_carry_out));
  _1_2 u_1_2 (.Input(Number), .Out(n1_2_out));  // open: Carry_out
  _1_2 u_1_3 (.Input(Number), .Out(n1_3_out));  // open: Carry_out
  _1_2 u_1_4 (.Input(Number), .Out(n1_4_out));  // open: Carry_out
  _1_2 u_1_5 (.Input(Number), .Out(n1_5_out));  // open: Carry_out
  _1_2 u_1_6 (.Input(Number), .Out(n1_6_out));  // open: Carry_out
  _1_2 u_1_7 (.Input(Number), .Out(n1_7_out));  // open: Carry_out
  _1_2 u_1_8 (.Input(n1_2_out), .Out(n1_8_out), .Carry_out(n1_8_carry_out));
  _1_2 u_1_9 (.Input(n1_10_out), .Out(n1_9_out), .Carry_out(n1_9_carry_out));
  _1_2 u_1_10 (.Input(n1_3_out), .Out(n1_10_out));  // open: Carry_out
  _1_2 u_1_11 (.Input(n1_4_out), .Out(n1_11_out));  // open: Carry_out
  _1_2 u_1_12 (.Input(n1_11_out), .Out(n1_12_out));  // open: Carry_out
  _1_2 u_1_13 (.Input(n1_5_out), .Out(n1_13_out));  // open: Carry_out
  _1_2 u_1_14 (.Input(n1_13_out), .Out(n1_14_out));  // open: Carry_out
  _1_2 u_1_15 (.Input(n1_6_out), .Out(n1_15_out));  // open: Carry_out
  _1_2 u_1_16 (.Input(n1_15_out), .Out(n1_16_out));  // open: Carry_out
  _1_2 u_1_17 (.Input(n1_7_out), .Out(n1_17_out));  // open: Carry_out
  _1_2 u_1_18 (.Input(n1_17_out), .Out(n1_18_out));  // open: Carry_out
  or or_1 (or_1_out, Shift_By[3], Shift_By[4], Shift_By[5], Shift_By[6], Shift_By[7]);
  _1_2 u_1_19 (.Input(n1_12_out), .Out(n1_19_out), .Carry_out(n1_19_carry_out));
  _1_2 u_1_20 (.Input(n1_21_out), .Out(n1_20_out), .Carry_out(n1_20_carry_out));
  _1_2 u_1_21 (.Input(n1_14_out), .Out(n1_21_out));  // open: Carry_out
  _1_2 u_1_22 (.Input(n1_16_out), .Out(n1_22_out));  // open: Carry_out
  _1_2 u_1_23 (.Input(n1_22_out), .Out(n1_23_out));  // open: Carry_out
  _1_2 u_1_24 (.Input(n1_18_out), .Out(n1_24_out));  // open: Carry_out
  _1_2 u_1_25 (.Input(n1_24_out), .Out(n1_25_out));  // open: Carry_out
  not not_1 (not_1_out, or_1_out);
  _1_2 u_1_26 (.Input(n1_23_out), .Out(n1_26_out), .Carry_out(n1_26_carry_out));
  _1_2 u_1_27 (.Input(n1_25_out), .Out(n1_27_out));  // open: Carry_out
  _1_2 u_1_28 (.Input(n1_27_out), .Out(n1_28_out), .Carry_out(n1_28_carry_out));
  _8_bit_8x1_mux u_8_bit_8x1_mux_1 (
    .D1(Number), .D2(n1_1_out), .D3(n1_8_out), .D4(n1_9_out), .D5(n1_19_out), .D6(n1_20_out), .D7(n1_26_out),
    .D8(n1_28_out), .Selector(Shift_By[2:0]), .Output(n8_bit_8x1_mux_1_output));
  Zeroer zeroer_1 (.Zero(not_1_out), .Number(n8_bit_8x1_mux_1_output), .Output(Output));
  _1_bit_8x1_mux u_1_bit_8x1_mux_1 (
    .D1(1'b0), .D2(n1_1_carry_out), .D3(n1_8_carry_out), .D4(n1_9_carry_out), .D5(n1_19_carry_out),
    .D6(n1_20_carry_out), .D7(n1_26_carry_out), .D8(n1_28_carry_out), .S1(Shift_By[2:0]), .Output(Carry));
endmodule

// MUL
module _8_bit_mul (
  input  [7:0] A,
  input  [7:0] B,
  output [7:0] out_3,
  output Carry,
  output Overflow
);

  wire [7:0] n8_bit_adder_subtracter_1_result, n8_bit_adder_subtracter_2_result,
       n8_bit_adder_subtracter_3_result, n8_bit_adder_subtracter_5_result, n8_bit_adder_subtracter_6_result,
       n8_bit_adder_subtracter_7_result, n8_bit_shl_1_output, n8_bit_shl_2_output, n8_bit_shl_3_output,
       n8_bit_shl_4_output, n8_bit_shl_5_output, n8_bit_shl_6_output, n8_bit_shl_7_output, zeroer_1_output,
       zeroer_2_output, zeroer_3_output, zeroer_4_output, zeroer_5_output, zeroer_6_output, zeroer_7_output,
       zeroer_8_output;

  Zeroer zeroer_1 (.Zero(A[7]), .Number(B), .Output(zeroer_1_output));
  _8_bit_shl u_8_bit_shl_1 (.Shift_By(8'h7), .Number(zeroer_1_output), .Output(n8_bit_shl_1_output));  // open: Carry
  Zeroer zeroer_2 (.Zero(A[6]), .Number(B), .Output(zeroer_2_output));
  _8_bit_shl u_8_bit_shl_2 (.Shift_By(8'h6), .Number(zeroer_2_output), .Output(n8_bit_shl_2_output));  // open: Carry
  _8_bit_shl u_8_bit_shl_3 (.Shift_By(8'h5), .Number(zeroer_3_output), .Output(n8_bit_shl_3_output));  // open: Carry
  Zeroer zeroer_3 (.Zero(A[5]), .Number(B), .Output(zeroer_3_output));
  _8_bit_Adder_Subtracter u_8_bit_adder_subtracter_1 (
    .Add_Sub_Control(1'b0), .Result(n8_bit_adder_subtracter_1_result), .A(n8_bit_shl_2_output),
    .B(n8_bit_shl_1_output));  // open: Carry_out, Overflow
  Zeroer zeroer_4 (.Zero(A[4]), .Number(B), .Output(zeroer_4_output));
  _8_bit_shl u_8_bit_shl_4 (.Shift_By(8'h4), .Number(zeroer_4_output), .Output(n8_bit_shl_4_output));  // open: Carry
  Zeroer zeroer_5 (.Zero(A[3]), .Number(B), .Output(zeroer_5_output));
  _8_bit_Adder_Subtracter u_8_bit_adder_subtracter_2 (
    .Add_Sub_Control(1'b0), .Result(n8_bit_adder_subtracter_2_result), .A(n8_bit_shl_4_output),
    .B(n8_bit_shl_3_output));  // open: Carry_out, Overflow
  _8_bit_shl u_8_bit_shl_5 (.Shift_By(8'h3), .Number(zeroer_5_output), .Output(n8_bit_shl_5_output));  // open: Carry
  Zeroer zeroer_6 (.Zero(A[2]), .Number(B), .Output(zeroer_6_output));
  _8_bit_Adder_Subtracter u_8_bit_adder_subtracter_3 (
    .Add_Sub_Control(1'b0), .Result(n8_bit_adder_subtracter_3_result), .A(n8_bit_adder_subtracter_2_result),
    .B(n8_bit_adder_subtracter_1_result));  // open: Carry_out, Overflow
  _8_bit_Adder_Subtracter u_8_bit_adder_subtracter_4 (
    .Add_Sub_Control(1'b0), .Result(out_3), .A(n8_bit_adder_subtracter_7_result),
    .B(n8_bit_adder_subtracter_3_result), .Carry_out(Carry), .Overflow(Overflow));
  _8_bit_shl u_8_bit_shl_6 (.Shift_By(8'h2), .Number(zeroer_6_output), .Output(n8_bit_shl_6_output));  // open: Carry
  Zeroer zeroer_7 (.Zero(A[1]), .Number(B), .Output(zeroer_7_output));
  _8_bit_shl u_8_bit_shl_7 (.Shift_By(8'h1), .Number(zeroer_7_output), .Output(n8_bit_shl_7_output));  // open: Carry
  _8_bit_Adder_Subtracter u_8_bit_adder_subtracter_5 (
    .Add_Sub_Control(1'b0), .Result(n8_bit_adder_subtracter_5_result), .A(n8_bit_shl_6_output),
    .B(n8_bit_shl_5_output));  // open: Carry_out, Overflow
  Zeroer zeroer_8 (.Zero(A[0]), .Number(B), .Output(zeroer_8_output));
  _8_bit_Adder_Subtracter u_8_bit_adder_subtracter_6 (
    .Add_Sub_Control(1'b0), .Result(n8_bit_adder_subtracter_6_result), .A(zeroer_8_output),
    .B(n8_bit_shl_7_output));  // open: Carry_out, Overflow
  _8_bit_Adder_Subtracter u_8_bit_adder_subtracter_7 (
    .Add_Sub_Control(1'b0), .Result(n8_bit_adder_subtracter_7_result), .A(n8_bit_adder_subtracter_6_result),
    .B(n8_bit_adder_subtracter_5_result));  // open: Carry_out, Overflow
endmodule

// DIV
module _8_bit_div (
  input  [7:0] Dividend,
  input  [7:0] Divisior,
  output [7:0] Quotient,
  output Overflow,
  output Carry
);

  wire sub_1_negative, sub_2_negative, sub_3_negative, sub_4_negative, sub_5_negative, sub_6_negative,
       sub_7_negative, sub_8_negative;
  wire [7:0] sub_1_result, sub_2_result, sub_4_result, sub_5_result, sub_6_result, sub_7_result,
       update_dividend_1_result, update_dividend_2_result, update_dividend_3_result,
       update_dividend_4_result, update_dividend_5_result, update_dividend_6_result,
       update_dividend_7_result, update_quotient_1_out_3, update_quotient_2_out_3, update_quotient_3_out_3,
       update_quotient_4_out_3, update_quotient_5_out_3, update_quotient_6_out_3, update_quotient_7_out_3;

  sub sub_1 (.A({{7{1'b0}}, Dividend[7]}), .B(Divisior), .Result(sub_1_result), .Negative(sub_1_negative));
  Update_dividend update_dividend_1 (
    .Original_dividend_bit(Dividend[6]), .Pre_subtraction({{7{1'b0}}, Dividend[7]}),
    .Post_subtratction(sub_1_result), .Result(update_dividend_1_result));
  update_quotient update_quotient_1 (.Shift_in(sub_1_negative), .Quotient({8{1'b0}}), .out_3(update_quotient_1_out_3));
  sub sub_2 (.A(update_dividend_1_result), .B(Divisior), .Result(sub_2_result), .Negative(sub_2_negative));
  update_quotient update_quotient_2 (
    .Shift_in(sub_2_negative), .Quotient(update_quotient_1_out_3), .out_3(update_quotient_2_out_3));
  Update_dividend update_dividend_2 (
    .Original_dividend_bit(Dividend[5]), .Pre_subtraction(update_dividend_1_result),
    .Post_subtratction(sub_2_result), .Result(update_dividend_2_result));
  sub sub_3 (.A(update_dividend_2_result), .B(Divisior), .Result(update_dividend_2_result), .Negative(sub_3_negative));
  update_quotient update_quotient_3 (
    .Shift_in(sub_3_negative), .Quotient(update_quotient_2_out_3), .out_3(update_quotient_3_out_3));
  Update_dividend update_dividend_3 (
    .Original_dividend_bit(Dividend[4]), .Pre_subtraction(update_dividend_2_result),
    .Post_subtratction(update_dividend_2_result), .Result(update_dividend_3_result));
  sub sub_4 (.A(update_dividend_3_result), .B(Divisior), .Result(sub_4_result), .Negative(sub_4_negative));
  update_quotient update_quotient_4 (
    .Shift_in(sub_4_negative), .Quotient(update_quotient_3_out_3), .out_3(update_quotient_4_out_3));
  Update_dividend update_dividend_4 (
    .Original_dividend_bit(Dividend[3]), .Pre_subtraction(update_dividend_3_result),
    .Post_subtratction(sub_4_result), .Result(update_dividend_4_result));
  sub sub_5 (.A(update_dividend_4_result), .B(Divisior), .Result(sub_5_result), .Negative(sub_5_negative));
  update_quotient update_quotient_5 (
    .Shift_in(sub_5_negative), .Quotient(update_quotient_4_out_3), .out_3(update_quotient_5_out_3));
  Update_dividend update_dividend_5 (
    .Original_dividend_bit(Dividend[2]), .Pre_subtraction(update_dividend_4_result),
    .Post_subtratction(sub_5_result), .Result(update_dividend_5_result));
  sub sub_6 (.A(update_dividend_5_result), .B(Divisior), .Result(sub_6_result), .Negative(sub_6_negative));
  update_quotient update_quotient_6 (
    .Shift_in(sub_6_negative), .Quotient(update_quotient_5_out_3), .out_3(update_quotient_6_out_3));
  Update_dividend update_dividend_6 (
    .Original_dividend_bit(Dividend[1]), .Pre_subtraction(update_dividend_5_result),
    .Post_subtratction(sub_6_result), .Result(update_dividend_6_result));
  sub sub_7 (.A(update_dividend_6_result), .B(Divisior), .Result(sub_7_result), .Negative(sub_7_negative));
  update_quotient update_quotient_7 (
    .Shift_in(sub_7_negative), .Quotient(update_quotient_6_out_3), .out_3(update_quotient_7_out_3));
  Update_dividend update_dividend_7 (
    .Original_dividend_bit(Dividend[0]), .Pre_subtraction(update_dividend_6_result),
    .Post_subtratction(sub_7_result), .Result(update_dividend_7_result));
  sub sub_8 (.A(update_dividend_7_result), .B(Divisior), .Negative(sub_8_negative));  // open: Result
  update_quotient update_quotient_8 (.Shift_in(sub_8_negative), .Quotient(update_quotient_7_out_3), .out_3(Quotient));
endmodule

// <<
module _1 (
  input  [7:0] Number,
  output [7:0] out_2,
  output Carry_out
);


  assign Carry_out = Number[7];
  assign out_2 = {Number[6:0], 1'b0};
endmodule

module Zeroer (
  input  Zero,
  input  [7:0] Number,
  output [7:0] Output
);

  and and_1 (Output[0], Number[0], Zero);
  and and_2 (Output[1], Number[1], Zero);
  and and_3 (Output[2], Number[2], Zero);
  and and_4 (Output[3], Number[3], Zero);
  and and_5 (Output[4], Number[4], Zero);
  and and_6 (Output[5], Number[5], Zero);
  and and_7 (Output[6], Number[6], Zero);
  and and_8 (Output[7], Number[7], Zero);
endmodule

// >>
module _1_2 (
  input  [7:0] Input,
  output [7:0] Out,
  output Carry_out
);


  assign Carry_out = Input[0];
  assign Out = {1'b0, Input[7:1]};
endmodule

module circuit (
  input  [7:0] A,
  input  [7:0] A_2,
  output out_3
);

  wire not_1_out, not_2_out, or_1_out;
  wire [7:0] n8_bit_adder_subtracter_1_result;

  _8_bit_Adder_Subtracter u_8_bit_adder_subtracter_1 (
    .Add_Sub_Control(1'b1), .Result(n8_bit_adder_subtracter_1_result), .A(A), .B(A_2));  // open: Carry_out, Overflow
  or or_1 (or_1_out, n8_bit_adder_subtracter_1_result[0], n8_bit_adder_subtracter_1_result[1], n8_bit_adder_subtracter_1_result[2], n8_bit_adder_subtracter_1_result[3], n8_bit_adder_subtracter_1_result[4], n8_bit_adder_subtracter_1_result[5], n8_bit_adder_subtracter_1_result[6], n8_bit_adder_subtracter_1_result[7]);
  not not_1 (not_1_out, or_1_out);
  not not_2 (not_2_out, n8_bit_adder_subtracter_1_result[7]);
  or or_2 (out_3, not_1_out, not_2_out);
endmodule

module _1_bit_2x1_mux (
  input  S1,
  input  D1,
  input  D2,
  output Output
);

  wire and_1_out, and_2_out, not_1_out;

  not not_1 (not_1_out, S1);
  and and_1 (and_1_out, D1, not_1_out);
  and and_2 (and_2_out, D2, S1);
  or or_1 (Output, and_1_out, and_2_out);
endmodule

// SUB
module sub (
  input  [7:0] A,
  input  [7:0] B,
  output [7:0] Result,
  output Negative
);

  _8_bit_Adder_Subtracter u_8_bit_adder_subtracter_1 (
    .Add_Sub_Control(1'b1), .Result({Negative, Result[6:0]}), .A(A), .B(B));  // open: Carry_out, Overflow

  assign Result[7] = Negative;
endmodule

// UPQ
module update_quotient (
  input  Shift_in,
  input  [7:0] Quotient,
  output [7:0] out_3
);

  wire [7:0] n1_1_out_2, n8_bit_adder_subtracter_1_result;

  _1 u_1_1 (.Number(Quotient), .out_2(n1_1_out_2));  // open: Carry_out
  _8_bit_Adder_Subtracter u_8_bit_adder_subtracter_1 (
    .Add_Sub_Control(1'b0), .Result(n8_bit_adder_subtracter_1_result), .A(n1_1_out_2), .B(8'h1));  // open: Carry_out, Overflow
  _8_bit_mux u_8_bit_mux_1 (
    .Control_Pin(Shift_in), .A(n1_1_out_2), .B(n8_bit_adder_subtracter_1_result), .Output(out_3));
endmodule

// UPD
module Update_dividend (
  input  Original_dividend_bit,
  input  [7:0] Pre_subtraction,
  input  [7:0] Post_subtratction,
  output [7:0] Result
);

  wire not_1_out;
  wire [7:0] n1_1_out_2, n1_2_out_2, n8_bit_adder_subtracter_1_result, n8_bit_adder_subtracter_2_result;

  _1 u_1_1 (.Number(Pre_subtraction), .out_2(n1_1_out_2));  // open: Carry_out
  _1 u_1_2 (.Number(Post_subtratction), .out_2(n1_2_out_2));  // open: Carry_out
  _8_bit_Adder_Subtracter u_8_bit_adder_subtracter_1 (
    .Add_Sub_Control(1'b0), .Result(n8_bit_adder_subtracter_1_result), .A(n1_1_out_2),
    .B({{7{1'b0}}, Original_dividend_bit}));  // open: Carry_out, Overflow
  not not_1 (not_1_out, Post_subtratction[7]);
  _8_bit_Adder_Subtracter u_8_bit_adder_subtracter_2 (
    .Add_Sub_Control(1'b0), .Result(n8_bit_adder_subtracter_2_result), .A(n1_2_out_2),
    .B({{7{1'b0}}, Original_dividend_bit}));  // open: Carry_out, Overflow
  _8_bit_mux u_8_bit_mux_1 (
    .Control_Pin(not_1_out), .A(n8_bit_adder_subtracter_1_result), .B(n8_bit_adder_subtracter_2_result),
    .Output(Result));
endmodule
